// Logisim project chap3.circ as structural Verilog: 7 circuits, main circuit main
module main (
  input  in_1,
  input  in_2,
  output out_3
);

  wire and_1_out, and_2_out, not_1_out, not_2_out;

  not not_1 (not_1_out, in_1);
  not not_2 (not_2_out, in_2);
  and and_1 (and_1_out, not_1_out, in_2);
  and and_2 (and_2_out, in_1, not_2_out);
  or or_1 (out_3, and_1_out, and_2_out);

  // Notes on the sheet:
  //   XOR
endmodule

module ADD_1_bit (
  input  a,
  input  b,
  input  c_in,
  output s,
  output c_out
);

  wire and_1_out, and_2_out, and_3_out, xor_1_out;

  xor xor_1 (xor_1_out, a, b);
  and and_1 (and_1_out, a, b);
  and and_2 (and_2_out, a, c_in);
  and and_3 (and_3_out, b, c_in);
  xor xor_2 (s, xor_1_out, c_in);
  or or_1 (c_out, and_1_out, and_2_out, and_3_out);
endmodule

module additioneur1bitBis (
  input  a,
  input  b,
  input  c_in,
  output s,
  output c_out
);

  wire and_1_out, and_2_out, and_3_out;

  xor odd_parity_1 (s, a, b, c_in);
  and and_1 (and_1_out, a, b);
  and and_2 (and_2_out, a, c_in);
  and and_3 (and_3_out, b, c_in);
  or or_1 (c_out, and_1_out, and_2_out, and_3_out);
endmodule

module ADD_8_bit (
  input  in_1,
  input  in_2,
  input  in_3,
  input  in_4,
  input  in_5,
  input  in_6,
  input  in_7,
  input  in_8,
  input  in_9,
  input  in_10,
  input  in_11,
  input  in_12,
  input  in_13,
  input  in_14,
  input  in_15,
  input  in_16,
  input  in_17,
  output out_18,
  output out_19,
  output out_20,
  output out_21,
  output out_22,
  output out_23,
  output out_24,
  output out_25,
  output out_26
);

  wire add_1_bit_1_c_out, add_1_bit_2_c_out, add_1_bit_3_c_out, add_1_bit_4_c_out, add_1_bit_5_c_out,
       add_1_bit_6_c_out, add_1_bit_7_c_out;

  ADD_1_bit add_1_bit_1 (.a(in_2), .b(in_3), .c_in(in_1), .s(out_18), .c_out(add_1_bit_1_c_out));
  ADD_1_bit add_1_bit_2 (.a(in_4), .b(in_5), .c_in(add_1_bit_1_c_out), .s(out_19), .c_out(add_1_bit_2_c_out));
  ADD_1_bit add_1_bit_3 (.a(in_6), .b(in_7), .c_in(add_1_bit_2_c_out), .s(out_20), .c_out(add_1_bit_3_c_out));
  ADD_1_bit add_1_bit_4 (.a(in_8), .b(in_9), .c_in(add_1_bit_3_c_out), .s(out_21), .c_out(add_1_bit_4_c_out));
  ADD_1_bit add_1_bit_5 (.a(in_10), .b(in_11), .c_in(add_1_bit_4_c_out), .s(out_22), .c_out(add_1_bit_5_c_out));
  ADD_1_bit add_1_bit_6 (.a(in_12), .b(in_13), .c_in(add_1_bit_5_c_out), .s(out_23), .c_out(add_1_bit_6_c_out));
  ADD_1_bit add_1_bit_7 (.a(in_14), .b(in_15), .c_in(add_1_bit_6_c_out), .s(out_24), .c_out(add_1_bit_7_c_out));
  ADD_1_bit add_1_bit_8 (.a(in_16), .b(in_17), .c_in(add_1_bit_7_c_out), .s(out_25), .c_out(out_26));
endmodule

module ADD_8_bit_V2 (
  input  [7:0] in_1,
  input  in_2,
  input  [7:0] in_3,
  output [7:0] out_4,
  output out_5
);

  wire add_1_bit_1_c_out, add_1_bit_2_c_out, add_1_bit_3_c_out, add_1_bit_4_c_out, add_1_bit_5_c_out,
       add_1_bit_6_c_out, add_1_bit_7_c_out;

  ADD_1_bit add_1_bit_1 (.a(in_1[0]), .b(in_3[0]), .c_in(in_2), .s(out_4[0]), .c_out(add_1_bit_1_c_out));
  ADD_1_bit add_1_bit_2 (.a(in_1[1]), .b(in_3[1]), .c_in(add_1_bit_1_c_out), .s(out_4[1]), .c_out(add_1_bit_2_c_out));
  ADD_1_bit add_1_bit_3 (.a(in_1[2]), .b(in_3[2]), .c_in(add_1_bit_2_c_out), .s(out_4[2]), .c_out(add_1_bit_3_c_out));
  ADD_1_bit add_1_bit_4 (.a(in_1[3]), .b(in_3[3]), .c_in(add_1_bit_3_c_out), .s(out_4[3]), .c_out(add_1_bit_4_c_out));
  ADD_1_bit add_1_bit_5 (.a(in_1[4]), .b(in_3[4]), .c_in(add_1_bit_4_c_out), .s(out_4[4]), .c_out(add_1_bit_5_c_out));
  ADD_1_bit add_1_bit_6 (.a(in_1[5]), .b(in_3[5]), .c_in(add_1_bit_5_c_out), .s(out_4[5]), .c_out(add_1_bit_6_c_out));
  ADD_1_bit add_1_bit_7 (.a(in_1[6]), .b(in_3[6]), .c_in(add_1_bit_6_c_out), .s(out_4[6]), .c_out(add_1_bit_7_c_out));
  ADD_1_bit add_1_bit_8 (.a(in_1[7]), .b(in_3[7]), .c_in(add_1_bit_7_c_out), .s(out_4[7]), .c_out(out_5));
endmodule

module ADD_SUB_8_bit (
  input  add_0___sub_1,
  input  [7:0] octet1,
  input  [7:0] octet2,
  output [7:0] out_4,
  output out_5
);

  wire [7:0] xor_octet_1_out_3;

  XOR_octet xor_octet_1 (.add_0___sub_1(add_0___sub_1), .octet(octet1), .out_3(xor_octet_1_out_3));
  ADD_8_bit_V2 add_8_bit_v2_1 (
    .in_1(xor_octet_1_out_3), .in_3(octet2), .out_4(out_4), .in_2(add_0___sub_1), .out_5(out_5));
endmodule

module XOR_octet (
  input  add_0___sub_1,
  input  [7:0] octet,
  output [7:0] out_3
);

  xor xor_1 (out_3[7], octet[7], add_0___sub_1);
  xor xor_2 (out_3[6], octet[6], add_0___sub_1);
  xor xor_3 (out_3[5], octet[5], add_0___sub_1);
  xor xor_4 (out_3[4], octet[4], add_0___sub_1);
  xor xor_5 (out_3[2], octet[2], add_0___sub_1);
  xor xor_6 (out_3[3], octet[3], add_0___sub_1);
  xor xor_7 (out_3[1], octet[1], add_0___sub_1);
  xor xor_8 (out_3[0], octet[0], add_0___sub_1);
endmodule
