// Logisim project chap4.circ as structural Verilog
module add (
  input  a,
  input  b,
  input  c_in,
  output s,
  output c_out
);

  wire and_1_out, and_2_out, and_3_out, xor_1_out;

  xor xor_1 (xor_1_out, a, b);
  and and_1 (and_1_out, a, b);
  and and_2 (and_2_out, a, c_in);
  and and_3 (and_3_out, b, c_in);
  xor xor_2 (s, xor_1_out, c_in);
  or or_1 (c_out, and_1_out, and_2_out, and_3_out);
endmodule

module add_octet (
  input  [7:0] in_1,
  input  in_2,
  input  [7:0] in_3,
  output [7:0] out_4,
  output out_5
);

  wire add_1_c_out, add_2_c_out, add_3_c_out, add_4_c_out, add_5_c_out, add_6_c_out, add_7_c_out;

  add add_1 (.a(in_1[0]), .b(in_3[0]), .c_in(in_2), .s(out_4[0]), .c_out(add_1_c_out));
  add add_2 (.a(in_1[1]), .b(in_3[1]), .c_in(add_1_c_out), .s(out_4[1]), .c_out(add_2_c_out));
  add add_3 (.a(in_1[2]), .b(in_3[2]), .c_in(add_2_c_out), .s(out_4[2]), .c_out(add_3_c_out));
  add add_4 (.a(in_1[3]), .b(in_3[3]), .c_in(add_3_c_out), .s(out_4[3]), .c_out(add_4_c_out));
  add add_5 (.a(in_1[4]), .b(in_3[4]), .c_in(add_4_c_out), .s(out_4[4]), .c_out(add_5_c_out));
  add add_6 (.a(in_1[5]), .b(in_3[5]), .c_in(add_5_c_out), .s(out_4[5]), .c_out(add_6_c_out));
  add add_7 (.a(in_1[6]), .b(in_3[6]), .c_in(add_6_c_out), .s(out_4[6]), .c_out(add_7_c_out));
  add add_8 (.a(in_1[7]), .b(in_3[7]), .c_in(add_7_c_out), .s(out_4[7]), .c_out(out_5));
endmodule

module latch (
  input  E,
  input  Keep,
  output S
);

  Multiplexer #(.enable("false")) multiplexer_1 (.in0(E), .in1(S), .out(S), .sel(Keep));
endmodule

module flip_flop (
  input  E,
  input  Ck,
  output S
);

  wire multiplexer_1_out;

  Multiplexer #(.enable("false")) multiplexer_1 (.in0(E), .in1(multiplexer_1_out), .out(multiplexer_1_out), .sel(Ck));
  Multiplexer #(.enable("false")) multiplexer_2 (.in0(S), .in1(multiplexer_1_out), .out(S), .sel(Ck));
endmodule

module flip_flop_reset (
  input  Reset,
  input  E,
  input  Ck,
  output S
);

  wire and_1_out, not_1_out;

  not not_1 (not_1_out, Reset);
  and and_1 (and_1_out, not_1_out, E);
  flip_flop flip_flop_1 (.E(and_1_out), .S(S), .Ck(Ck));
endmodule

module flip_flop_enable (
  input  Reset,
  input  E,
  input  Ck,
  input  Enable,
  output S
);

  wire flip_flop_reset_1_s;

  flip_flop_reset flip_flop_reset_1 (.Reset(Reset), .E(E), .S(flip_flop_reset_1_s), .Ck(Ck));
  Multiplexer #(.enable("false")) multiplexer_1 (.in0(flip_flop_reset_1_s), .in1(S), .out(S), .sel(Enable));
endmodule

module registre_octet (
  input  [7:0] E,
  input  Reset,
  input  Ck,
  input  Enable,
  output [7:0] S
);

  flip_flop_enable flip_flop_enable_1 (.Reset(Reset), .E(E[7]), .S(S[7]), .Ck(Ck), .Enable(Enable));
  flip_flop_enable flip_flop_enable_2 (.Reset(Reset), .E(E[6]), .S(S[6]), .Ck(Ck), .Enable(Enable));
  flip_flop_enable flip_flop_enable_3 (.Reset(Reset), .E(E[5]), .S(S[5]), .Ck(Ck), .Enable(Enable));
  flip_flop_enable flip_flop_enable_4 (.Reset(Reset), .E(E[4]), .S(S[4]), .Ck(Ck), .Enable(Enable));
  flip_flop_enable flip_flop_enable_5 (.Reset(Reset), .E(E[3]), .S(S[3]), .Ck(Ck), .Enable(Enable));
  flip_flop_enable flip_flop_enable_6 (.Reset(Reset), .E(E[2]), .S(S[2]), .Ck(Ck), .Enable(Enable));
  flip_flop_enable flip_flop_enable_7 (.Reset(Reset), .E(E[1]), .S(S[1]), .Ck(Ck), .Enable(Enable));
  flip_flop_enable flip_flop_enable_8 (.Reset(Reset), .E(E[0]), .S(S[0]), .Ck(Ck), .Enable(Enable));
endmodule

module compteur (
  input  C_in,
  input  [7:0] Increment,
  input  Reset,
  output [7:0] S
);

  wire add_octet_1_out_5, clock_1_out;
  wire [7:0] add_octet_1_out_4;

  Clock clock_1 (.out(clock_1_out));
  add_octet add_octet_1 (.in_1(S), .in_3(Increment), .out_4(add_octet_1_out_4), .in_2(C_in), .out_5(add_octet_1_out_5));
  registre_octet registre_octet_1 (
    .E(add_octet_1_out_4), .Reset(Reset), .Ck(clock_1_out), .Enable(add_octet_1_out_5), .S(S));
endmodule

module ram (
  input  [7:0] in_1,
  input  [7:0] in_2,
  input  in_3,
  input  in_4,
  input  in_5,
  input  in_6,
  input  in_7,
  output [7:0] out_8
);

  RAM #(.bus("separate")) ram_1 (
    .addr(in_1), .din(in_2), .data(out_8), .str(in_3), .sel(in_5), .clk(in_7), .ld(in_6), .clr(in_4));
endmodule

module demux_1_vers2 (
  input  in_1,
  input  E,
  output out_3,
  output out_4
);

  xor xor_1 (out_3, in_1, E);
  not not_1 (out_4, out_3);
endmodule
