// Logisim project chap5.circ as structural Verilog
module fonctionTransition (
  input  reset,
  input  [1:0] S,
  input  go,
  input  pp,
  input  clock,
  output [1:0] S_prime
);

  wire and_1_out, and_2_out, and_3_out, and_4_out, and_5_out, and_6_out, and_7_out, and_8_out, not_1_out,
       not_2_out, not_3_out, not_4_out, not_5_out, not_6_out, not_7_out, not_8_out, or_1_out, or_2_out;

  not not_1 (not_1_out, reset);
  not not_2 (not_2_out, reset);
  and and_1 (and_1_out, not_1_out, S[0]);
  and and_2 (and_2_out, not_2_out, S[1]);
  not not_3 (not_3_out, and_1_out);
  not not_4 (not_4_out, and_2_out);
  not not_5 (not_5_out, and_2_out);
  not not_6 (not_6_out, pp);
  not not_7 (not_7_out, and_1_out);
  not not_8 (not_8_out, and_2_out);
  and and_3 (and_3_out, not_3_out, not_4_out, go);
  and and_4 (and_4_out, not_5_out, not_6_out, and_1_out);
  and and_5 (and_5_out, and_2_out, not_7_out);
  and and_6 (and_6_out, go, and_2_out, and_1_out);
  and and_7 (and_7_out, and_1_out, not_8_out);
  and and_8 (and_8_out, and_2_out, and_1_out, go);
  or or_1 (or_1_out, and_3_out, and_4_out, and_5_out, and_6_out);
  or or_2 (or_2_out, and_7_out, and_8_out);
  Multiplexer #(.enable("false")) multiplexer_1 (.in0(S_prime[0]), .in1(or_1_out), .out(S_prime[0]), .sel(clock));
  Multiplexer #(.enable("false")) multiplexer_2 (.in0(S_prime[1]), .in1(or_2_out), .out(S_prime[1]), .sel(clock));
endmodule

module fonctionSortie (
  input  [1:0] S,
  output OK,
  output LX,
  output LQ,
  output LN,
  output LP,
  output RX,
  output RP
);

  wire not_1_out, not_2_out, not_3_out;

  not not_1 (not_1_out, S[0]);
  not not_2 (not_2_out, S[0]);
  not not_3 (not_3_out, S[1]);
  and and_1 (OK, S[0], S[1]);
  and and_2 (LQ, not_1_out, S[1]);
  and and_3 (LN, not_2_out, not_3_out);

  assign LP = LN;
  assign LX = LQ;
  assign RP = LN;
  assign RX = LN;
endmodule

module control (
);

  wire fonctionsortie_1_ln, fonctionsortie_1_lp, fonctionsortie_1_lq, fonctionsortie_1_lx,
       fonctionsortie_1_ok, fonctionsortie_1_rp, fonctionsortie_1_rx, fonctiontransition_1_p1,
       fonctiontransition_1_p2;
  wire [1:0] fonctiontransition_1_p5;

  // fonctionTransition fonctiontransition_1: pin names not known; wires that end beside it: fonctiontransition_1_p1, fonctiontransition_1_p2, fonctiontransition_1_p1, fonctiontransition_1_p2, fonctiontransition_1_p5
  fonctionSortie fonctionsortie_1 (
    .S(fonctiontransition_1_p5), .OK(fonctionsortie_1_ok), .LX(fonctionsortie_1_lx),
    .LQ(fonctionsortie_1_lq), .LN(fonctionsortie_1_ln), .LP(fonctionsortie_1_lp), .RX(fonctionsortie_1_rx),
    .RP(fonctionsortie_1_rp));
endmodule

module comparateur (
  input  [7:0] A,
  input  [7:0] B,
  output out_3
);

  Subtractor subtractor_1 (.a(A), .b(B), .bin(1'b0), .bout(out_3));  // open: out
endmodule

module Diviseur (
  input  Reset,
  input  Go,
  input  [7:0] N,
  input  [7:0] P,
  output ok,
  output [7:0] Q
);

  wire Clock_out, comparateur_1_out_3, LN, LP, LQ, LX, RQ, RX;
  wire [1:0] fonctiontransition_1_s_prime, register_5_q;
  wire [7:0] adder_1_out, register_1_q, register_2_q, register_3_q, register_4_q;

  Clock Clock (.out(Clock_out));
  Register register_1 (.D(N), .en(LN), .Q(register_1_q), .clk(Clock_out), .clr(1'b0));
  Register register_2 (.D(adder_1_out), .en(LX), .Q(register_2_q), .clk(Clock_out), .clr(RX));
  Register register_3 (.D(P), .en(LP), .Q(register_3_q), .clk(Clock_out), .clr(1'b0));
  Register register_4 (.D(Q), .en(LQ), .Q(register_4_q), .clk(Clock_out), .clr(RQ));
  fonctionTransition fonctiontransition_1 (
    .S(register_5_q), .go(Go), .pp(comparateur_1_out_3), .S_prime(fonctiontransition_1_s_prime),
    .clock(Clock_out), .reset(Reset));
  Register #(.width(2)) register_5 (
    .D(fonctiontransition_1_s_prime), .Q(register_5_q), .clk(Clock_out));  // open: en, clr
  Adder adder_1 (.a(register_2_q), .b(register_3_q), .out(adder_1_out), .cin(1'b0));  // open: cout
  Adder adder_2 (.a(8'h1), .b(register_4_q), .out(Q), .cin(1'b0));  // open: cout
  comparateur comparateur_1 (.A(adder_1_out), .B(register_1_q), .out_3(comparateur_1_out_3));
  fonctionSortie fonctionsortie_1 (.S(register_5_q), .OK(ok), .LX(LX), .LQ(LQ), .LN(LN), .LP(LP), .RX(RX), .RP(RQ));
endmodule
