// Logisim project cpu.circ as structural Verilog: 3 circuits, main circuit vonNeumanMachine
module vonNeumanMachine (
  input  in_1,
  input  in_2
);

  wire clock_1_out;
  wire [7:0] cpu_1_address, rom_1_data;

  CPU cpu_1 (.datain(rom_1_data), .address(cpu_1_address), .CK(clock_1_out), .rst(in_1));
  Clock clock_1 (.out(clock_1_out));
  ROM rom_1 (.addr(cpu_1_address), .data(rom_1_data), .sel(in_2));

  // Notes on the sheet:
  //   contents of rom_1 (hex, n*v repeats v):
  //   0 86 7f
endmodule

module CPU (
  input  [7:0] datain,
  input  CK,
  input  rst,
  output [7:0] address
);

  wire go_to, jump, loadIR, loadPC;
  wire [7:0] adder_1_out, adder_2_out, IR, multiplexer_1_out, multiplexer_2_out;

  FSM fsm_1 (.instr(IR), .CK(CK), .rst(rst), .LoadIR(loadIR), .LoadPC(loadPC), .got_to(go_to), .jump(jump));
  Register u_IR (.D(datain), .en(loadIR), .Q(IR), .clk(CK), .clr(rst));
  Adder adder_1 (.a(address), .b(8'h1), .out(adder_1_out), .cin(1'b0));  // open: cout
  Multiplexer #(.width(8), .enable("false")) multiplexer_1 (
    .in0(adder_1_out), .in1(datain), .out(multiplexer_1_out), .sel(go_to));
  Multiplexer #(.width(8), .enable("false")) multiplexer_2 (
    .in0(multiplexer_1_out), .in1(adder_2_out), .out(multiplexer_2_out), .sel(jump));
  Adder adder_2 (.a(address), .b({{4{IR[4]}}, IR[3:0]}), .out(adder_2_out), .cin(1'b0));  // open: cout
  // Probe on address
  Register PC (.D(multiplexer_2_out), .en(loadPC), .Q(address), .clk(CK), .clr(rst));

  // Other names for the same wires on the sheet: PC[7:0] = address
endmodule

module FSM (
  input  [7:0] instr,
  input  CK,
  input  rst,
  output LoadPC,
  output LoadIR,
  output got_to,
  output jump
);

  wire _1xx, _7f, and_1_out, and_3_out, and_4_out, and_5_out, d_ff_2_q, d_ff_4_q, d_ff_6_q, decode, n1xx,
       n7f, not_1_out, not_2_out, not_3_out, not_4_out, not_5_out, not_7_out, state_fetch;

  Comparator comparator_1 (.a(instr), .b(8'h7f), .eq(_7f));  // open: gt, lt
  not not_1 (not_1_out, instr[0]);
  not not_2 (not_2_out, instr[1]);
  and and_1 (and_1_out, not_1_out, not_2_out, not_3_out, not_4_out, not_5_out);
  not not_3 (not_3_out, instr[2]);
  not not_4 (not_4_out, instr[3]);
  not not_5 (not_5_out, instr[4]);
  not not_6 (n7f, _7f);
  not not_7 (not_7_out, and_1_out);
  not not_8 (n1xx, _1xx);
  and and_2 (_1xx, not_7_out, instr[7]);
  and and_3 (and_3_out, decode, n1xx, n7f);
  and and_4 (and_4_out, decode, _7f);
  and and_5 (and_5_out, decode, _1xx);
  D_Flip_Flop d_ff_1 (.clk(CK), .D(state_fetch), .Q(decode), .reset(rst));  // open: Qn, preset, en
  D_Flip_Flop d_ff_2 (.clk(CK), .D(and_3_out), .Q(d_ff_2_q), .preset(rst));  // open: Qn, en, reset
  D_Flip_Flop d_ff_3 (.clk(CK), .D(and_4_out), .Q(got_to), .reset(rst));  // open: Qn, preset, en
  D_Flip_Flop d_ff_4 (.clk(CK), .D(got_to), .Q(d_ff_4_q), .reset(rst));  // open: Qn, preset, en
  D_Flip_Flop d_ff_5 (.clk(CK), .D(and_5_out), .Q(jump), .reset(rst));  // open: Qn, preset, en
  D_Flip_Flop d_ff_6 (.clk(CK), .D(jump), .Q(d_ff_6_q), .reset(rst));  // open: Qn, preset, en
  or or_1 (state_fetch, d_ff_2_q, d_ff_4_q, d_ff_6_q);
  or or_2 (LoadPC, decode, jump, got_to);
  or or_3 (LoadIR, state_fetch, got_to);

  // Other names for the same wires on the sheet: go_to = got_to
endmodule
