// Logisim project mm_etu_nofsm_halfalu_composants_2016_2017.circ as structural Verilog: 5 circuits, main circuit Von Neumann machine
module Von_Neumann_machine (
  input  reset
);

  wire clock_out, cpu_1_m_we;
  wire [7:0] cpu_1_ma, cpu_1_mdo, ram_1_data;

  CPU cpu_1 (.MA(cpu_1_ma), .MDI(ram_1_data), .MDO(cpu_1_mdo), .M_we(cpu_1_m_we), .ck(clock_out), .reset(reset));
  Clock clock (.out(clock_out));
  // Probe on cpu_1_ma
  // Probe on cpu_1_mdo
  // Probe on ram_1_data
  RAM #(.bus("separate")) ram_1 (
    .addr(cpu_1_ma), .din(cpu_1_mdo), .data(ram_1_data), .str(cpu_1_m_we), .sel(1'b1), .clk(clock_out),
    .ld(1'b1));  // open: clr

  // Notes on the sheet:
  //   processor
  //   system bus
  //   address
  //   data: CPU to memory
  //   data: memory to CPU
  //   control: 1 means "write"
  //   memory
endmodule

module CPU (
  input  [7:0] MDI,
  input  ck,
  input  reset,
  output [7:0] MA,
  output [7:0] MDO,
  output M_we
);

  wire fsm_1_dofetch, fsm_1_doja, fsm_1_dojr, fsm_1_memwrite, fsm_1_wecst, fsm_1_wedestreg, fsm_1_weflags,
       fsm_1_weir, fsm_1_wepc;
  wire [2:0] data_path_1_flags;
  wire [7:0] data_path_1_ir;

  FSM fsm_1 (
    .Instruction(data_path_1_ir), .flags(data_path_1_flags), .weIR(fsm_1_weir), .doFetch(fsm_1_dofetch),
    .memwrite(fsm_1_memwrite), .weDestReg(fsm_1_wedestreg), .wePC(fsm_1_wepc), .weCST(fsm_1_wecst),
    .doJA(fsm_1_doja), .doJR(fsm_1_dojr), .weFlags(fsm_1_weflags), .reset(reset), .clk(ck));
  Data_Path data_path_1 (
    .weIR(fsm_1_weir), .doFetch(fsm_1_dofetch), .memwrite(fsm_1_memwrite), .weDestReg(fsm_1_wedestreg),
    .wePC(fsm_1_wepc), .weCST(fsm_1_wecst), .doJA(fsm_1_doja), .doJR(fsm_1_dojr), .weFlags(fsm_1_weflags),
    .IR(data_path_1_ir), .MA(MA), .MDI(MDI), .MDO(MDO), .M_we(M_we), .Flags(data_path_1_flags), .ck(ck),
    .reset(reset));

  // Notes on the sheet:
  //   FSM (Automate)
  //   Data Path
  //   Instruction
  //   Flags
  //   (memory address)
  //   (data in from mem)
  //   (data out to mem)
  //   (memory write enable)
endmodule

module Data_Path (
  input  weIR,
  input  doFetch,
  input  memwrite,
  input  weDestReg,
  input  wePC,
  input  weCST,
  input  doJA,
  input  doJR,
  input  weFlags,
  input  [7:0] MDI,
  input  ck,
  input  reset,
  output [7:0] IR,
  output [7:0] MA,
  output [7:0] MDO,
  output M_we,
  output [2:0] Flags
);

  wire comparator_1_eq, weA, weB;
  wire [2:0] alu_1_flags;
  wire [7:0] adder_1_out, alu_1_out, multiplexer_2_out, multiplexer_3_out, multiplexer_4_out,
       multiplexer_5_out, regA, regB, regCST, regPC;

  // Probe on MDO
  Multiplexer #(.width(8), .enable("false")) multiplexer_1 (.in0(regA), .in1(regB), .out(MDO), .sel(IR[1]));
  // Probe on multiplexer_2_out
  Multiplexer #(.width(8), .enable("false")) multiplexer_2 (
    .in0(regA), .in1(regCST), .out(multiplexer_2_out), .sel(IR[2]));
  ALU alu_1 (
    .arg1(MDO), .arg2(multiplexer_2_out), .out(alu_1_out), .flags(alu_1_flags), .codeop(IR[6:3]),
    .arg2s(IR[2]));
  Multiplexer #(.width(8), .enable("false")) multiplexer_3 (
    .in0(8'h1), .in1({{4{IR[4]}}, IR[3:0]}), .out(multiplexer_3_out), .sel(doJR));
  Adder adder_1 (.a(regPC), .b(multiplexer_3_out), .out(adder_1_out));  // open: cin, cout
  // Probe on Flags
  Register #(.width(3)) u_flags (.D(alu_1_flags), .en(weFlags), .Q(Flags), .clk(ck), .clr(reset));
  // Probe on alu_1_out
  Multiplexer #(.width(8), .enable("false")) multiplexer_4 (
    .in0(alu_1_out), .in1(MDI), .out(multiplexer_4_out), .sel(comparator_1_eq));
  Comparator #(.width(4)) comparator_1 (.a(IR[6:3]), .b(4'b1101), .eq(comparator_1_eq));  // open: gt, lt
  Multiplexer #(.width(8), .enable("false")) multiplexer_5 (
    .in0(adder_1_out), .in1(regCST), .out(multiplexer_5_out), .sel(doJA));
  Register u_IR (.D(MDI), .en(weIR), .Q(IR), .clk(ck), .clr(reset));
  Register CST (.D(MDI), .en(weCST), .Q(regCST), .clk(ck), .clr(reset));
  // Probe on multiplexer_5_out
  Register PC (.D(multiplexer_5_out), .en(wePC), .Q(regPC), .clk(ck), .clr(reset));
  Register A (.D(multiplexer_4_out), .en(weA), .Q(regA), .clk(ck), .clr(reset));
  Register B (.D(multiplexer_4_out), .en(weB), .Q(regB), .clk(ck), .clr(reset));
  and and_1 (weA, ~IR[0], weDestReg);  // AND_Gate
  and and_2 (weB, IR[0], weDestReg);
  // Probe on multiplexer_2_out
  // Probe on MDI
  Multiplexer #(.width(8), .enable("false")) multiplexer_6 (
    .in0(multiplexer_2_out), .in1(regPC), .out(MA), .sel(doFetch));

  assign M_we = memwrite;

  // Other names for the same wires on the sheet: destS = IR[0]; offset[4:0] = IR[4:0]; arg1S = IR[1]; arg2S = IR[2];
  //   opcode[3:0] = IR[6:3]

  // Notes on the sheet:
  //   (Instruction)
  //   (memory address)
  //   (data out to mem)
  //   (memory write enable)
  //   (data in from mem)
endmodule

module ALU (
  input  [7:0] arg1,
  input  [7:0] arg2,
  input  [3:0] codeop,
  input  arg2s,
  output [2:0] flags,
  output [7:0] out
);

  wire carryAdd, carrySub;
  wire [7:0] adder_1_out, and_1_out, or_1_out, subtractor_1_out, xor_1_out, xor_2_out;

  Adder adder_1 (.a(arg1), .b(arg2), .out(adder_1_out), .cin(1'b0), .cout(carryAdd));
  Subtractor subtractor_1 (.a(arg1), .b(arg2), .out(subtractor_1_out), .bin(1'b0), .bout(carrySub));
  assign and_1_out = arg1 & arg2;  // AND_Gate and_1, 8 bits wide
  assign or_1_out = arg1 | arg2;  // OR_Gate or_1, 8 bits wide
  assign xor_1_out = arg1 ^ arg2;  // XOR_Gate xor_1, 8 bits wide
  assign xor_2_out = arg1 ^ {8{arg2s}};  // XOR_Gate xor_2, 8 bits wide
  Multiplexer #(.select(4), .width(8), .enable("false")) multiplexer_1 (
    .in0(adder_1_out), .in1(subtractor_1_out), .in2(and_1_out), .in3(or_1_out), .in4(xor_1_out),
    .in5({1'b0, arg1[7:1]}), .in8(xor_2_out), .in9(arg2), .out({flags[2], out[6:0]}), .sel(codeop));  // open: in6, in7, in10, in11, in12, in13, in14, in15
  Comparator comparator_1 (.a({flags[2], out[6:0]}), .b({8{1'b0}}), .eq(flags[0]));  // open: gt, lt
  Multiplexer #(.select(4), .enable("false")) multiplexer_2 (
    .in0(carryAdd), .in1(carrySub), .in2(1'b0), .in3(1'b0), .in4(1'b0), .in5(arg1[0]), .in6(1'b0),
    .in7(1'b0), .in8(1'b0), .in9(1'b0), .in10(1'b0), .in11(1'b0), .in12(1'b0), .in13(1'b0), .in14(1'b0),
    .in15(1'b0), .out(flags[1]), .sel(codeop));

  assign out[7] = flags[2];

  // Notes on the sheet:
  //   0000 add
  //   0001 sub
  //   0110 cmp
  //   0010 and
  //   0011 or
  //   0100 xor
  //   0101 lsr
  //   1000 passthrough/invert arg1
  //   1001 passthrough arg2
endmodule

module FSM (
  input  [7:0] Instruction,
  input  [2:0] flags,
  input  clk,
  input  reset,
  output doFetch,
  output weIR,
  output weDestReg,
  output wePC,
  output weCST,
  output weFlags,
  output doJR,
  output doJA,
  output memwrite
);

  wire and_1_out, and_2_out, and_3_out, and_5_out, and_6_out, and_7_out, and_8_out, InstrDecode, JA,
       not_1_out, not_2_out, not_3_out, not_4_out, not_5_out, or_1_out, or_2_out, or_3_out;

  not not_1 (not_1_out, Instruction[7]);
  not not_2 (not_2_out, Instruction[7]);
  and and_1 (and_1_out, InstrDecode, not_2_out, Instruction[3]);
  and and_2 (and_2_out, InstrDecode, Instruction[7]);
  and and_3 (and_3_out, InstrDecode, not_1_out, Instruction[3]);
  and and_4 (JA, Instruction[4], Instruction[5], Instruction[6]);
  not not_3 (not_3_out, and_2_out);
  or or_1 (or_1_out, and_3_out, JA);
  not not_4 (not_4_out, or_1_out);
  not not_5 (not_5_out, JA);
  and and_5 (and_5_out, InstrDecode, Instruction[7]);
  or or_2 (or_2_out, and_1_out, JA);
  and and_6 (and_6_out, not_3_out, not_4_out);
  and and_7 (and_7_out, weCST, JA);
  and and_8 (and_8_out, weCST, not_5_out);
  or or_3 (or_3_out, weDestReg, doJA, doJR);
  D_Flip_Flop d_ff_1 (.clk(clk), .D(doFetch), .Q(InstrDecode), .reset(reset));  // open: Qn, preset, en
  D_Flip_Flop d_ff_2 (.clk(clk), .D(and_5_out), .Q(doJR), .reset(reset));  // open: Qn, preset, en
  D_Flip_Flop d_ff_3 (.clk(clk), .D(or_2_out), .Q(Instruction[3]), .reset(reset));  // open: Qn, preset, en
  D_Flip_Flop d_ff_4 (.clk(clk), .D(and_6_out), .Q(weDestReg), .reset(reset));  // open: Qn, preset, en
  D_Flip_Flop d_ff_5 (.clk(clk), .D(Instruction[3]), .Q(weCST), .reset(reset));  // open: Qn, preset, en
  D_Flip_Flop d_ff_6 (.clk(clk), .D(and_7_out), .Q(doJA), .reset(reset));  // open: Qn, preset, en
  D_Flip_Flop d_ff_7 (.clk(clk), .D(and_8_out), .Q(weDestReg), .reset(reset));  // open: Qn, preset, en
  D_Flip_Flop d_ff_8 (.clk(clk), .D(or_3_out), .Q(doFetch), .preset(reset));  // open: Qn, en, reset
  or or_4 (wePC, weDestReg, Instruction[3], doJA, doJR);

  assign memwrite = 1'b0;
  assign weFlags = weDestReg;
  assign weIR = doFetch;

  // Other names for the same wires on the sheet: ConstFetch = weCST; InstrFetch = doFetch; IncrPC = Instruction[3];
  //   JR = Instruction[7]; RegWrite = weDestReg

  // Notes on the sheet:
  //   ERREUR CI DESSOUS
endmodule
